// Logisim project RegisterFile.circ as structural Verilog: 1 circuit, main circuit RegisterFile
module RegisterFile (
  input  [3:0] WriteData,
  input  WriteEnable,
  input  [2:0] WriteReg,
  input  Clock,
  input  [2:0] ReadReg1,
  input  [2:0] ReadReg2,
  input  Reset,
  output [3:0] ReadData1,
  output [3:0] ReadData2
);

  wire decoder_1_out0, decoder_1_out1, decoder_1_out2, decoder_1_out4, decoder_1_out5, decoder_1_out6,
       decoder_1_out7;
  wire [3:0] REG_0_q, REG_1_q, REG_2_q, REG_3_q, REG_4_q, REG_5_q, REG_6_q, REG_7_q;

  Decoder #(.select(3)) decoder_1 (
    .out0(decoder_1_out0), .out1(decoder_1_out1), .out2(decoder_1_out2), .out3(Reset), .out4(decoder_1_out4),
    .out5(decoder_1_out5), .out6(decoder_1_out6), .out7(decoder_1_out7), .sel(WriteReg), .en(WriteEnable));
  Register #(.width(4)) REG_0 (.D(WriteData), .en(decoder_1_out0), .clk(Clock), .Q(REG_0_q), .clr(Reset));
  Register #(.width(4)) REG_2 (.D(WriteData), .en(decoder_1_out2), .clk(Clock), .Q(REG_2_q), .clr(Reset));
  Register #(.width(4)) REG_4 (.D(WriteData), .en(decoder_1_out4), .clk(Clock), .Q(REG_4_q), .clr(Reset));
  Register #(.width(4)) REG_6 (.D(WriteData), .en(decoder_1_out6), .clk(Clock), .Q(REG_6_q), .clr(Reset));
  Register #(.width(4)) REG_1 (.D(WriteData), .en(decoder_1_out1), .clk(Clock), .Q(REG_1_q), .clr(Reset));
  Register #(.width(4)) REG_3 (.D(WriteData), .en(Reset), .clk(Clock), .Q(REG_3_q), .clr(Reset));
  Register #(.width(4)) REG_5 (.D(WriteData), .en(decoder_1_out5), .clk(Clock), .Q(REG_5_q), .clr(Reset));
  Register #(.width(4)) REG_7 (.D(WriteData), .en(decoder_1_out7), .clk(Clock), .Q(REG_7_q), .clr(Reset));
  Multiplexer #(.select(3), .width(4)) multiplexer_1 (
    .in0(REG_0_q), .in1(REG_1_q), .in2(REG_2_q), .in3(REG_3_q), .in4(REG_4_q), .in5(REG_5_q), .in6(REG_6_q),
    .in7(REG_7_q), .out(ReadData1), .sel(ReadReg1));
  Multiplexer #(.select(3), .width(4)) multiplexer_2 (
    .in0(REG_0_q), .in1(REG_1_q), .in2(REG_2_q), .in3(REG_3_q), .in4(REG_4_q), .in5(REG_5_q), .in6(REG_6_q),
    .in7(REG_7_q), .out(ReadData2), .sel(ReadReg2));
endmodule
